// Logisim project CPU.circ as structural Verilog: 13 circuits, main circuit main
module main (
  input  [7:0] INPUT,
  output [15:0] out_2,
  output [15:0] out_3,
  output [15:0] out_4,
  output [15:0] out_5,
  output [15:0] out_6,
  output [3:0] out_7,
  output [15:0] out_8,
  output [15:0] out_9,
  output [7:0] OUTPUT
);

  wire alu_1_out_7, and_1_out, button_1_out, clock_1_out, cu_1_ac_2, cu_1_clr, cu_1_clr_2, cu_1_clr_3,
       cu_1_clr_4, cu_1_clr_5, cu_1_en, cu_1_fgi_2, cu_1_inc, cu_1_inc_2, cu_1_inc_3, cu_1_inc_4, cu_1_inc_5,
       cu_1_inc_6, cu_1_ir_2, cu_1_ld, cu_1_ld_2, cu_1_ld_3, cu_1_ld_4, cu_1_ld_5, cu_1_ld_6, cu_1_m_load,
       cu_1_outr_en, cu_1_q, cu_1_r_en, cu_1_r_q, cu_1_r_reset, cu_1_reset, cu_1_reset_2, cu_1_s, cu_1_tr,
       E_q, FGI_q, FGO_q, IEN_q, not_1_out, or_1_out, or_2_out, or_3_out, or_4_out, or_5_out, or_6_out,
       or_7_out, or_8_out, or_9_out, or_10_out, R_q, S_q;
  wire [2:0] cu_1_bus_select;
  wire [3:0] cu_1_out_26;
  wire [7:0] INPR_q;
  wire [11:0] AR_out_6, n16to12_1_out_2, n16to12_2_out_2, PC_out_6;
  wire [15:0] alu_1_out_6, controlled_buffer_1_out, ram_1_data;

  _16to12 u_16to12_1 (.in_1(out_2), .out_2(n16to12_1_out_2));
  _16to12 u_16to12_2 (.in_1(out_2), .out_2(n16to12_2_out_2));
  Register INPR (.D(INPUT), .Q(INPR_q), .clk(and_1_out));  // open: en, clr
  ALU alu_1 (.INPR(INPR_q), .DR(out_5), .AC(out_6), .E(E_q), .in_5(out_7), .out_6(alu_1_out_6), .out_7(alu_1_out_7));
  Register OUTR (.D(out_2[7:0]), .en(cu_1_outr_en), .Q(OUTPUT), .clk(and_1_out));  // open: clr
  Register12 AR (
    .INP(n16to12_1_out_2), .LOAD(cu_1_ld), .CLK(and_1_out), .CLR(or_1_out), .INCR(cu_1_inc), .out_6(AR_out_6));
  Register12 PC (
    .INP(n16to12_2_out_2), .LOAD(cu_1_ld_2), .CLK(and_1_out), .CLR(or_2_out), .INCR(cu_1_inc_2),
    .out_6(PC_out_6));
  Register16 DR (
    .INP(out_2), .LOAD(cu_1_ld_4), .CLK(and_1_out), .CLR(or_3_out), .INCR(cu_1_inc_4), .out_7(out_5));  // open: out_6
  assign controlled_buffer_1_out = cu_1_m_load ? ram_1_data : 16'bz;  // Controlled_Buffer controlled_buffer_1
  RAM #(.addrWidth(12), .dataWidth(16)) ram_1 (
    .addr(AR_out_6), .data(ram_1_data), .sel(1'b1), .clk(and_1_out), .ld(cu_1_m_load));  // open: clr
  assign ram_1_data = not_1_out ? out_2 : 16'bz;  // Controlled_Buffer controlled_buffer_2
  not not_1 (not_1_out, cu_1_m_load);
  _12to16 u_12to16_1 (.in_1(AR_out_6), .out_2(out_3));
  _12to16 u_12to16_2 (.in_1(PC_out_6), .out_2(out_4));
  Register16 AC (
    .INP(alu_1_out_6), .LOAD(cu_1_ac_2), .CLK(and_1_out), .CLR(or_4_out), .INCR(cu_1_inc_5), .out_7(out_6));  // open: out_6
  Register16 IR (
    .INP(out_2), .LOAD(cu_1_ld_3), .CLK(and_1_out), .CLR(or_5_out), .INCR(cu_1_inc_3), .out_7(out_8));  // open: out_6
  Register16 TR (
    .INP(out_2), .LOAD(cu_1_ld_6), .CLK(and_1_out), .CLR(or_6_out), .INCR(cu_1_inc_6), .out_7(out_9));  // open: out_6
  Multiplexer #(.select(3), .width(16)) multiplexer_1 (
    .in1(out_3), .in2(out_4), .in3(out_5), .in4(out_6), .in5(out_8), .in6(out_9),
    .in7(controlled_buffer_1_out), .out(out_2), .sel(cu_1_bus_select), .en(1'b1));  // open: in0
  or or_1 (or_1_out, button_1_out, cu_1_clr);
  or or_2 (or_2_out, button_1_out, cu_1_ir_2);
  or or_3 (or_3_out, button_1_out, cu_1_clr_4);
  or or_4 (or_4_out, button_1_out, cu_1_tr);
  or or_5 (or_5_out, button_1_out, cu_1_clr_2);
  or or_6 (or_6_out, button_1_out, cu_1_clr_5);
  D_Flip_Flop E (.clk(and_1_out), .D(alu_1_out_7), .Q(E_q), .en(cu_1_ld_5), .reset(cu_1_clr_3));  // open: Qn, preset
  D_Flip_Flop S (.clk(clock_1_out), .Q(S_q), .reset(cu_1_s));  // open: D, Qn, preset, en
  D_Flip_Flop IEN (.clk(and_1_out), .D(cu_1_q), .Q(IEN_q), .en(cu_1_en), .reset(or_7_out));  // open: Qn, preset
  D_Flip_Flop FGI (.clk(and_1_out), .Q(FGI_q), .reset(or_8_out));  // open: D, Qn, preset, en
  D_Flip_Flop FGO (.clk(and_1_out), .Q(FGO_q), .reset(or_9_out));  // open: D, Qn, preset, en
  D_Flip_Flop R (.clk(and_1_out), .D(cu_1_r_q), .Q(R_q), .en(cu_1_r_en), .reset(or_10_out));  // open: Qn, preset
  and and_1 (and_1_out, S_q, clock_1_out);
  Clock clock_1 (.out(clock_1_out));
  or or_7 (or_7_out, button_1_out, cu_1_reset);
  or or_8 (or_8_out, button_1_out, cu_1_fgi_2);
  or or_9 (or_9_out, button_1_out, cu_1_reset_2);
  or or_10 (or_10_out, button_1_out, cu_1_r_reset);
  Button button_1 (.out(button_1_out));
  CU cu_1 (
    .IR(out_8), .DR(out_5), .E(E_q), .AC(out_6), .FGI(FGI_q), .FGO(FGO_q), .IEN(IEN_q), .R(R_q),
    .LD(cu_1_ld), .INC(cu_1_inc), .CLR(cu_1_clr), .LD_2(cu_1_ld_2), .INC_2(cu_1_inc_2), .IR_2(cu_1_ir_2),
    .LD_3(cu_1_ld_3), .INC_3(cu_1_inc_3), .CLR_2(cu_1_clr_2), .LD_4(cu_1_ld_4), .LD_5(cu_1_ld_5),
    .INC_4(cu_1_inc_4), .CLR_3(cu_1_clr_3), .CLR_4(cu_1_clr_4), .AC_2(cu_1_ac_2), .INC_5(cu_1_inc_5),
    .TR(cu_1_tr), .LD_6(cu_1_ld_6), .INC_6(cu_1_inc_6), .CLR_5(cu_1_clr_5), .BUS_SELECT(cu_1_bus_select),
    .S(cu_1_s), .ALU_OPCODE(out_7), .M_LOAD(cu_1_m_load), .EN(cu_1_en), .Q(cu_1_q), .RESET(cu_1_reset),
    .FGI_2(cu_1_fgi_2), .RESET_2(cu_1_reset_2), .OUTR_EN(cu_1_outr_en), .R_EN(cu_1_r_en), .R_Q(cu_1_r_q),
    .R_RESET(cu_1_r_reset), .in_5(and_1_out), .out_26(cu_1_out_26), .in_4(button_1_out));
  Hex_Digit_Display hex_digit_display_1 (.value(cu_1_out_26));  // open: dp
endmodule

module ALU (
  input  [7:0] INPR,
  input  [15:0] DR,
  input  [15:0] AC,
  input  E,
  input  [3:0] in_5,
  output [15:0] out_6,
  output out_7
);

  wire adder_1_cout, cil_1_out_4, cir_1_out_3, xor_1_out;
  wire [15:0] adder_1_out, and_16bit_1_out_3, cil_1_out_3, cir_1_out_4, comp_16bit_1_out_2;

  Adder #(.width(16)) adder_1 (.a(DR), .b(AC), .out(adder_1_out), .cout(adder_1_cout));  // open: cin
  AND_16bit and_16bit_1 (.AC(DR), .out_3(and_16bit_1_out_3), .DR(AC));
  COMP_16bit comp_16bit_1 (.in_1(AC), .out_2(comp_16bit_1_out_2));
  xor xor_1 (xor_1_out, E, 1'b1);
  CIL cil_1 (.in_1(E), .in_2(AC), .out_3(cil_1_out_3), .out_4(cil_1_out_4));
  CIR cir_1 (.in_1(AC), .in_2(E), .out_3(cir_1_out_3), .out_4(cir_1_out_4));
  Multiplexer #(.select(4), .width(16)) multiplexer_1 (
    .in0(AC), .in1(adder_1_out), .in2(and_16bit_1_out_3), .in3(comp_16bit_1_out_2), .in4(cil_1_out_3),
    .in5(cir_1_out_4), .in6(AC), .in7({{8{1'b0}}, INPR}), .in8(DR), .out(out_6), .sel(in_5), .en(1'b1));  // open: in9, in10, in11, in12, in13, in14, in15
  Multiplexer #(.select(4)) multiplexer_2 (
    .in0(E), .in1(adder_1_cout), .in2(E), .in3(E), .in4(cil_1_out_4), .in5(cir_1_out_3), .in6(xor_1_out),
    .in7(E), .in8(E), .out(out_7), .sel(in_5), .en(1'b1));  // open: in9, in10, in11, in12, in13, in14, in15

  // Notes on the sheet:
  //   Input to AC
  //   ADD
  //   AND
  //   AC CMP
  //   E CMP
  //   CIL
  //   CIR
endmodule

module Register16 (
  input  [15:0] INP,
  input  LOAD,
  input  CLK,
  input  CLR,
  input  INCR,
  output [15:0] out_6,
  output [15:0] out_7
);

  wire not_1_out, or_1_out, or_2_out, or_3_out, or_4_out;
  wire [15:0] adder_1_out, register_2_q;

  assign out_6 = or_3_out ? adder_1_out : 16'bz;  // Controlled_Buffer controlled_buffer_1
  assign out_6 = not_1_out ? INP : 16'bz;  // Controlled_Buffer controlled_buffer_2
  not not_1 (not_1_out, or_3_out);
  or or_1 (or_1_out, CLK, 1'b0);
  or or_2 (or_2_out, CLR, 1'b0);
  or or_3 (or_3_out, INCR, 1'b0);
  Register #(.width(16)) register_1 (.D(out_6), .en(or_4_out), .Q(out_7), .clk(or_1_out), .clr(or_2_out));
  or or_4 (or_4_out, LOAD, or_3_out);
  Register #(.width(16)) register_2 (.Q(register_2_q));  // open: D, en, clk, clr
  Adder #(.width(16)) adder_1 (.a(out_7), .b(register_2_q), .out(adder_1_out), .cin(or_3_out));  // open: cout
endmodule

module Register12 (
  input  [11:0] INP,
  input  LOAD,
  input  CLK,
  input  CLR,
  input  INCR,
  output [11:0] out_6
);

  wire not_1_out, or_1_out, or_2_out, or_3_out, or_4_out;
  wire [11:0] adder_1_out, controlled_buffer_1_out, register_2_q;

  assign controlled_buffer_1_out = or_3_out ? adder_1_out : 12'bz;  // Controlled_Buffer controlled_buffer_1
  assign controlled_buffer_1_out = not_1_out ? INP : 12'bz;  // Controlled_Buffer controlled_buffer_2
  not not_1 (not_1_out, or_3_out);
  or or_1 (or_1_out, CLK, 1'b0);
  or or_2 (or_2_out, CLR, 1'b0);
  buf or_3 (or_3_out, INCR);  // OR_Gate
  Register #(.width(12)) register_1 (
    .D(controlled_buffer_1_out), .en(or_4_out), .Q(out_6), .clk(or_1_out), .clr(or_2_out));
  or or_4 (or_4_out, LOAD, or_3_out);
  Register #(.width(12)) register_2 (.Q(register_2_q));  // open: D, en, clk, clr
  Adder #(.width(12)) adder_1 (.a(out_6), .b(register_2_q), .out(adder_1_out), .cin(or_3_out));  // open: cout
endmodule

module _12to16 (
  input  [11:0] in_1,
  output [15:0] out_2
);

  Register #(.width(4)) register_1 (.Q(out_2[15:12]));  // open: D, en, clk, clr

  assign out_2[11:0] = in_1;
endmodule

module _16to12 (
  input  [15:0] in_1,
  output [11:0] out_2
);


  assign out_2 = in_1[11:0];
endmodule

module _16to8 (
  input  [15:0] in_1,
  output [7:0] out_2
);


  assign out_2 = in_1[7:0];
endmodule

module AND_16bit (
  input  [15:0] AC,
  input  [15:0] DR,
  output [15:0] out_3
);

  and and_1 (out_3[0], AC[0], DR[0]);
  and and_2 (out_3[1], AC[1], DR[1]);
  and and_3 (out_3[2], AC[2], DR[2]);
  and and_4 (out_3[3], AC[3], DR[3]);
  and and_5 (out_3[4], AC[4], DR[4]);
  and and_6 (out_3[5], AC[5], DR[5]);
  and and_7 (out_3[6], AC[6], DR[6]);
  and and_8 (out_3[7], AC[7], DR[7]);
  and and_9 (out_3[8], AC[8], DR[8]);
  and and_10 (out_3[9], AC[9], DR[9]);
  and and_11 (out_3[10], AC[10], DR[10]);
  and and_12 (out_3[11], AC[11], DR[11]);
  and and_13 (out_3[12], AC[12], DR[12]);
  and and_14 (out_3[13], AC[13], DR[13]);
  and and_15 (out_3[14], AC[14], DR[14]);
  and and_16 (out_3[15], AC[15], DR[15]);
endmodule

module COMP_16bit (
  input  [15:0] in_1,
  output [15:0] out_2
);

  xor xor_1 (out_2[0], 1'b1, in_1[0]);
  xor xor_2 (out_2[1], 1'b1, in_1[1]);
  xor xor_3 (out_2[2], 1'b1, in_1[2]);
  xor xor_4 (out_2[3], 1'b1, in_1[3]);
  xor xor_5 (out_2[4], 1'b1, in_1[4]);
  xor xor_6 (out_2[5], 1'b1, in_1[5]);
  xor xor_7 (out_2[6], 1'b1, in_1[6]);
  xor xor_8 (out_2[7], 1'b1, in_1[7]);
  xor xor_9 (out_2[8], 1'b1, in_1[8]);
  xor xor_10 (out_2[9], 1'b1, in_1[9]);
  xor xor_11 (out_2[10], 1'b1, in_1[10]);
  xor xor_12 (out_2[11], 1'b1, in_1[11]);
  xor xor_13 (out_2[12], 1'b1, in_1[12]);
  xor xor_14 (out_2[13], 1'b1, in_1[13]);
  xor xor_15 (out_2[14], 1'b1, in_1[14]);
  xor xor_16 (out_2[15], 1'b1, in_1[15]);
endmodule

module CIL (
  input  in_1,
  input  [15:0] in_2,
  output [15:0] out_3,
  output out_4
);


  assign out_3 = {in_2[14:0], in_1};
  assign out_4 = in_2[15];
endmodule

module CIR (
  input  [15:0] in_1,
  input  in_2,
  output out_3,
  output [15:0] out_4
);


  assign out_3 = in_1[0];
  assign out_4 = {in_2, in_1[15:1]};
endmodule

module CU (
  input  [15:0] IR,
  input  [15:0] DR,
  input  E,
  input  in_4,
  input  in_5,
  input  [15:0] AC,
  input  FGI,
  input  FGO,
  input  IEN,
  input  R,
  output LD,
  output INC,
  output CLR,
  output LD_2,
  output INC_2,
  output IR_2,
  output LD_3,
  output INC_3,
  output CLR_2,
  output LD_4,
  output LD_5,
  output INC_4,
  output CLR_3,
  output CLR_4,
  output AC_2,
  output [3:0] out_26,
  output INC_5,
  output TR,
  output LD_6,
  output INC_6,
  output CLR_5,
  output [2:0] BUS_SELECT,
  output S,
  output [3:0] ALU_OPCODE,
  output M_LOAD,
  output EN,
  output Q,
  output RESET,
  output FGI_2,
  output RESET_2,
  output OUTR_EN,
  output R_EN,
  output R_Q,
  output R_RESET
);

  wire _0_2_out, _1_out, _2_out, and_1_out, and_3_out, and_4_out, and_5_out, and_6_out, and_7_out, and_8_out,
       and_9_out, and_10_out, and_11_out, and_12_out, and_14_out, and_15_out, and_16_out, and_17_out,
       and_18_out, and_19_out, and_20_out, and_21_out, D3T4_out, D4T4_out, D5T4_out, D5T6_out, D6T4_out,
       D6T6_out, D7_prime_I_out, D7I_out, D7I_prime_out, decoder_1_out0, decoder_1_out1, decoder_1_out2,
       decoder_1_out3, decoder_1_out4, decoder_1_out5, decoder_1_out6, decoder_1_out7, decoder_2_out7, I_q,
       I_qn, Indirect_out, M_out, nor_1_out, not_1_out, not_2_out, or_1_out, or_2_out, or_3_out, or_4_out,
       or_5_out, or_6_out, or_7_out, or_8_out, or_9_out, or_10_out, or_11_out, or_13_out, or_16_out,
       or_18_out, or_19_out, or_20_out, or_22_out, p_out, pB6_out, pB8_out, pB9_out, r_out, rB1_out, rB2_out,
       rB3_out, rB4_out, rB6_out, rB7_out, rB8_out, rB9_out, RT3_out, SC_2_out, sign_1_zero, sign_2_neg,
       sign_2_pos, sign_2_zero;
  wire [6:0] decoder_2_out0;

  Counter #(.width(4), .max('hf)) SC (
    .load(1'b0), .count(1'b1), .Q(out_26), .clk(in_5), .clr(SC_2_out));  // open: D, carry
  or SC_2 (SC_2_out, and_4_out, or_1_out, or_2_out);
  Decoder #(.select(4)) decoder_1 (
    .out0(decoder_1_out0), .out1(decoder_1_out1), .out2(decoder_1_out2), .out3(decoder_1_out3),
    .out4(decoder_1_out4), .out5(decoder_1_out5), .out6(decoder_1_out6), .out7(decoder_1_out7), .sel(out_26),
    .en(1'b1));  // open: out8, out9, out10, out11, out12, out13, out14, out15
  SIGN sign_1 (.in_1(DR), .ZERO(sign_1_zero));  // open: POS, NEG
  or or_1 (or_1_out, RT3_out, and_5_out);
  or or_2 (or_2_out, in_4, or_7_out);
  Decoder #(.select(3)) decoder_2 (
    .out0(decoder_2_out0[0]), .out1(decoder_2_out0[1]), .out2(decoder_2_out0[2]), .out3(decoder_2_out0[3]),
    .out4(decoder_2_out0[4]), .out5(decoder_2_out0[5]), .out6(decoder_2_out0[6]), .out7(decoder_2_out7),
    .sel(IR[14:12]), .en(1'b1));
  D_Flip_Flop I (.clk(in_5), .D(IR[15]), .Q(I_q), .Qn(I_qn), .en(and_1_out));  // open: preset, reset
  and and_1 (and_1_out, decoder_1_out2, not_2_out);
  nor nor_1 (nor_1_out, decoder_1_out0, decoder_1_out1, and_1_out);
  and and_2 (LD_3, decoder_1_out1, not_2_out);
  and and_3 (and_3_out, decoder_1_out0, not_2_out);
  and rB0 (S, r_out, IR[0]);
  and rB1 (rB1_out, r_out, IR[1]);
  and rB2 (rB2_out, r_out, IR[2]);
  and rB3 (rB3_out, r_out, IR[3]);
  and rB4 (rB4_out, r_out, IR[4]);
  and rB5 (INC_5, r_out, IR[5]);
  and rB6 (rB6_out, r_out, IR[6]);
  and rB7 (rB7_out, r_out, IR[7]);
  and rB8 (rB8_out, r_out, IR[8]);
  and rB9 (rB9_out, r_out, IR[9]);
  and rB10 (CLR_3, r_out, IR[10]);
  and rB11 (TR, r_out, IR[11]);
  or or_3 (or_3_out, decoder_2_out0[3], decoder_2_out0[4]);
  or or_4 (or_4_out, decoder_2_out0[0], decoder_2_out0[1], decoder_2_out0[2]);
  or or_5 (or_5_out, decoder_2_out0[5], decoder_2_out0[6]);
  and pB6 (pB6_out, p_out, IR[6]);
  and pB7 (EN, p_out, IR[7]);
  and pB8 (pB8_out, p_out, IR[8]);
  and pB9 (pB9_out, p_out, IR[9]);
  and pB10 (OUTR_EN, p_out, IR[10]);
  and pB11 (FGI_2, p_out, IR[11]);
  not not_1 (not_1_out, decoder_2_out7);
  and and_4 (and_4_out, decoder_1_out4, D7I_out);
  and p (p_out, decoder_1_out3, D7I_out);
  not not_2 (not_2_out, R);
  and RT0 (CLR, R, decoder_1_out0);
  and RT1 (IR_2, R, decoder_1_out1);
  and RT2 (R_RESET, R, decoder_1_out2);
  and RT3 (RT3_out, R, decoder_1_out3);
  // AND_Gate D7_prime_I_prime has open pins: in0=not_1_out, in1=I_qn, out=open
  and D7I_prime (D7I_prime_out, decoder_2_out7, I_qn);
  and D7_prime_I (D7_prime_I_out, not_1_out, I_q);
  and D7I (D7I_out, decoder_2_out7, I_q);
  and u_r (r_out, decoder_1_out3, D7I_prime_out);
  and and_5 (and_5_out, D7I_prime_out, decoder_1_out4);
  and and_6 (and_6_out, decoder_1_out5, decoder_2_out0[0]);
  and and_7 (and_7_out, decoder_1_out5, or_3_out);
  and and_8 (and_8_out, decoder_1_out6, or_4_out);
  and and_9 (and_9_out, decoder_1_out7, or_5_out);
  and and_10 (and_10_out, pB8_out, FGO);
  and and_11 (and_11_out, pB9_out, FGI);
  or or_6 (or_6_out, FGI, FGO);
  and Indirect (Indirect_out, D7_prime_I_out, decoder_1_out3);
  SIGN sign_2 (.in_1(AC), .ZERO(sign_2_zero), .POS(sign_2_pos), .NEG(sign_2_neg));
  and and_12 (and_12_out, decoder_1_out5, decoder_2_out0[1]);
  or or_7 (or_7_out, and_7_out, and_8_out, and_9_out);
  or or_8 (or_8_out, and_10_out, and_11_out);
  and and_13 (R_EN, or_6_out, IEN, nor_1_out);
  or or_9 (or_9_out, decoder_2_out0[0], decoder_2_out0[2], decoder_2_out0[1]);
  and D5T6 (D5T6_out, decoder_1_out6, decoder_2_out0[5]);
  and D5T5 (INC, decoder_1_out5, decoder_2_out0[5]);
  and D5T4 (D5T4_out, decoder_2_out0[5], decoder_1_out4);
  and D4T4 (D4T4_out, decoder_1_out4, decoder_2_out0[4]);
  and and_14 (and_14_out, E, rB1_out);
  and and_15 (and_15_out, sign_2_zero, rB2_out);
  or or_10 (or_10_out, and_14_out, and_15_out, and_16_out, and_17_out);
  and and_16 (and_16_out, sign_2_neg, rB3_out);
  and and_17 (and_17_out, sign_2_pos, rB4_out);
  and and_18 (and_18_out, decoder_1_out5, decoder_2_out0[2]);
  and and_19 (and_19_out, or_9_out, decoder_1_out4);
  and D3T4 (D3T4_out, decoder_1_out4, decoder_2_out0[3]);
  and and_20 (and_20_out, sign_1_zero, D6T6_out);
  and D6T6 (D6T6_out, decoder_1_out6, decoder_2_out0[6]);
  and D6T5 (INC_4, decoder_1_out5, decoder_2_out0[6]);
  or or_11 (or_11_out, D6T6_out, D4T4_out, D5T6_out);
  or M (M_out, and_19_out, D6T4_out, LD_3);
  or or_12 (RESET, pB6_out, R_RESET);
  or or_13 (or_13_out, or_8_out, LD_3);
  and D6T4 (D6T4_out, decoder_1_out4, decoder_2_out0[6]);
  or or_14 (LD, and_3_out, and_1_out, Indirect_out);
  or or_15 (LD_2, D5T6_out, D4T4_out);
  or or_16 (or_16_out, or_10_out, and_20_out, or_13_out);
  or or_17 (LD_4, and_19_out, D6T4_out);
  or or_18 (or_18_out, D5T4_out, D6T6_out);
  or or_19 (or_19_out, M_out, and_1_out, OUTR_EN, Indirect_out, D3T4_out);
  or _0 (ALU_OPCODE[0], rB7_out, and_12_out, _0_2_out);
  or _0_2 (_0_2_out, FGI_2, rB9_out);
  or _1 (_1_out, FGI_2, rB8_out);
  or _2 (_2_out, rB6_out, FGI_2);
  or or_20 (or_20_out, rB6_out, rB7_out, rB9_out, FGI_2);
  nor nor_2 (M_LOAD, D6T6_out, D5T4_out, D3T4_out, 1'b0, IR_2);
  and and_21 (and_21_out, or_9_out, decoder_1_out5);
  or _1_2 (ALU_OPCODE[1], and_6_out, rB9_out, _1_out);
  or _2_2 (ALU_OPCODE[2], rB8_out, rB7_out, _2_out);
  buf _3 (ALU_OPCODE[3], and_18_out);  // OR_Gate
  or or_21 (AC_2, and_21_out, or_20_out);
  or or_22 (or_22_out, IR_2, CLR);
  or or_23 (LD_5, and_12_out, rB8_out);
  or or_24 (BUS_SELECT[1], or_18_out, and_3_out, M_out, Indirect_out, or_22_out);
  or or_25 (INC_2, or_16_out, R_RESET);
  or or_26 (BUS_SELECT[2], or_19_out, IR_2);
  or or_27 (BUS_SELECT[0], or_11_out, M_out, Indirect_out, and_1_out);

  assign CLR_2 = 1'b0;
  assign CLR_4 = 1'b0;
  assign CLR_5 = 1'b0;
  assign INC_3 = 1'b0;
  assign INC_6 = 1'b0;
  assign LD_6 = CLR;
  assign Q = EN;
  assign R_Q = R_EN;
  assign RESET_2 = OUTR_EN;

  // Notes on the sheet:
  //   IEN
  //   RESET
  //   FGO
  //   CLR
  //   AR
  //   DR
  //   PC
  //   CLR
  //   LD
  //   CLR
  //   E
endmodule

module SIGN (
  input  [15:0] in_1,
  output ZERO,
  output POS,
  output NEG
);

  wire not_2_out, or_1_out;

  or or_1 (or_1_out, in_1[0], in_1[1], in_1[2], in_1[3], in_1[4], in_1[5], in_1[6], in_1[7], in_1[9], in_1[10], in_1[11], in_1[12], in_1[13], in_1[14], in_1[15], in_1[8]);
  not not_1 (ZERO, or_1_out);
  not not_2 (not_2_out, in_1[15]);
  and and_1 (POS, or_1_out, not_2_out);

  assign NEG = in_1[15];
endmodule
