// Logisim project Calculator.circ as structural Verilog: 8 circuits, main circuit main
module main (
  input  A0,
  input  A1,
  input  A2,
  input  A3,
  input  B0,
  input  B1,
  input  B2,
  input  B3,
  input  C0,
  input  C1,
  output S0,
  output S1,
  output S2,
  output S3
);

  wire adder_subtractor_1_s0, adder_subtractor_1_s1, adder_subtractor_1_s2, adder_subtractor_1_s3, and_1_out,
       and_2_out, and_3_out, and_4_out, and_5_out, and_6_out, and_7_out, and_8_out, and_9_out, and_10_out,
       and_11_out, and_12_out, and_13_out, and_14_out, and_15_out, and_16_out, and_17_out, and_18_out,
       and_19_out, and_20_out, and_21_out, and_22_out, and_23_out, and_24_out, and_25_out, and_26_out,
       and_27_out, and_28_out, and_29_out, and_30_out, and_31_out, and_32_out, and_33_out, button_1_out,
       full_divisor_1_c0, full_divisor_1_c1, full_divisor_1_c2, full_divisor_1_c3, multiplier_1_s0,
       multiplier_1_s1, multiplier_1_s2, multiplier_1_s3, not_1_out, not_2_out;

  Button button_1 (.out(button_1_out));
  and and_1 (and_1_out, A0, button_1_out);
  and and_2 (and_2_out, A1, button_1_out);
  and and_3 (and_3_out, A2, button_1_out);
  and and_4 (and_4_out, A3, button_1_out);
  and and_5 (and_5_out, B0, button_1_out);
  and and_6 (and_6_out, B1, button_1_out);
  and and_7 (and_7_out, B2, button_1_out);
  and and_8 (and_8_out, B3, button_1_out);
  and and_9 (and_9_out, C0, button_1_out);
  and and_10 (and_10_out, C1, button_1_out);
  and and_11 (and_11_out, C0, not_1_out);
  not not_1 (not_1_out, C1);
  and and_12 (and_12_out, C0, C1);
  and and_13 (and_13_out, button_1_out, and_12_out);
  not not_2 (not_2_out, and_9_out);
  and and_14 (and_14_out, and_1_out, not_2_out);
  and and_15 (and_15_out, and_2_out, not_2_out);
  and and_16 (and_16_out, and_3_out, not_2_out);
  and and_17 (and_17_out, and_4_out, not_2_out);
  and and_18 (and_18_out, and_5_out, not_2_out);
  and and_19 (and_19_out, and_6_out, not_2_out);
  and and_20 (and_20_out, and_7_out, not_2_out);
  and and_21 (and_21_out, and_8_out, not_2_out);
  and and_22 (and_22_out, and_1_out, and_11_out);
  and and_23 (and_23_out, and_2_out, and_11_out);
  and and_24 (and_24_out, and_3_out, and_11_out);
  and and_25 (and_25_out, and_4_out, and_11_out);
  and and_26 (and_26_out, and_5_out, and_11_out);
  and and_27 (and_27_out, and_6_out, and_11_out);
  and and_28 (and_28_out, and_7_out, and_11_out);
  and and_29 (and_29_out, and_8_out, and_11_out);
  Multiplier multiplier_1 (
    .A0(and_22_out), .A1(and_23_out), .A2(and_24_out), .A3(and_25_out), .B0(and_26_out), .B1(and_27_out),
    .B2(and_28_out), .B3(and_29_out), .S0(multiplier_1_s0), .S1(multiplier_1_s1), .S2(multiplier_1_s2),
    .S3(multiplier_1_s3));
  Adder_Subtractor adder_subtractor_1 (
    .Subtract(and_10_out), .A0(and_14_out), .A1(and_15_out), .A2(and_16_out), .A3(and_17_out),
    .B0(and_18_out), .B1(and_19_out), .B2(and_20_out), .B3(and_21_out), .S0(adder_subtractor_1_s0),
    .S1(adder_subtractor_1_s1), .S2(adder_subtractor_1_s2), .S3(adder_subtractor_1_s3));
  Full_Divisor full_divisor_1 (
    .A0(and_1_out), .A1(and_2_out), .A2(and_3_out), .A3(and_4_out), .B0(and_5_out), .B1(and_6_out),
    .B2(and_7_out), .B3(and_8_out), .C3(full_divisor_1_c3), .C2(full_divisor_1_c2), .C1(full_divisor_1_c1),
    .C0(full_divisor_1_c0));
  and and_30 (and_30_out, full_divisor_1_c0, and_13_out);
  and and_31 (and_31_out, full_divisor_1_c1, and_13_out);
  and and_32 (and_32_out, full_divisor_1_c2, and_13_out);
  and and_33 (and_33_out, full_divisor_1_c3, and_13_out);
  or or_1 (S0, adder_subtractor_1_s0, multiplier_1_s0, and_30_out);
  or or_2 (S1, adder_subtractor_1_s1, multiplier_1_s1, and_31_out);
  or or_3 (S2, adder_subtractor_1_s2, multiplier_1_s2, and_32_out);
  or or_4 (S3, adder_subtractor_1_s3, multiplier_1_s3, and_33_out);

  // Notes on the sheet:
  //   Bits from low to high
  //   00: Sum(A+B)
  //   01:Mul(A*B)
  //   10:Subtract(A-B)
  //   11:Divide(A/B)
  //   Press Button to see result
endmodule

module Adder (
  input  A,
  input  B,
  input  CarryIn,
  output SUM,
  output CarryOut
);

  wire and_1_out, and_2_out, and_3_out;

  xor xor_1 (SUM, A, B, CarryIn);
  and and_1 (and_1_out, A, B);
  and and_2 (and_2_out, A, CarryIn);
  and and_3 (and_3_out, B, CarryIn);
  or or_1 (CarryOut, and_1_out, and_2_out, and_3_out);
endmodule

module Full_Adder (
  input  A0,
  input  B0,
  input  Carry,
  input  A1,
  input  B1,
  input  A2,
  input  B2,
  input  A3,
  input  B3,
  output S0,
  output S1,
  output S2,
  output S3
);

  wire adder_1_carryout, adder_2_carryout, adder_3_carryout, adder_4_carryout;

  Adder adder_1 (.A(A0), .B(B0), .CarryIn(Carry), .SUM(S0), .CarryOut(adder_1_carryout));
  Adder adder_2 (.A(A1), .B(B1), .CarryIn(adder_1_carryout), .SUM(S1), .CarryOut(adder_2_carryout));
  Adder adder_3 (.A(A2), .B(B2), .CarryIn(adder_2_carryout), .SUM(S2), .CarryOut(adder_3_carryout));
  Adder adder_4 (.A(A3), .B(B3), .CarryIn(adder_3_carryout), .SUM(S3), .CarryOut(adder_4_carryout));
  // also tied to GND on the sheet: adder_4_carryout
endmodule

module Adder_Subtractor (
  input  Subtract,
  input  A0,
  input  A1,
  input  A2,
  input  A3,
  input  B0,
  input  B1,
  input  B2,
  input  B3,
  output S0,
  output S1,
  output S2,
  output S3
);

  wire xor_1_out, xor_2_out, xor_3_out, xor_4_out;

  xor xor_1 (xor_1_out, Subtract, B0);
  xor xor_2 (xor_2_out, Subtract, B1);
  xor xor_3 (xor_3_out, Subtract, B2);
  xor xor_4 (xor_4_out, Subtract, B3);
  Full_Adder full_adder_1 (
    .A0(A0), .B0(xor_1_out), .Carry(Subtract), .A1(A1), .B1(xor_2_out), .A2(A2), .B2(xor_3_out), .A3(A3),
    .B3(xor_4_out), .S0(S0), .S1(S1), .S2(S2), .S3(S3));
endmodule

module Multiplier (
  input  A0,
  input  A1,
  input  A2,
  input  A3,
  input  B0,
  input  B1,
  input  B2,
  input  B3,
  output S0,
  output S1,
  output S2,
  output S3
);

  wire A0B0_out, A0B1_out, A0B2_out, A0B3_out, A1B0_out, A1B1_out, A1B2_out, A2B0_out, A2B1_out, A3B0_out,
       adder_subtractor_1_s0, adder_subtractor_1_s1, adder_subtractor_1_s2, adder_subtractor_1_s3,
       adder_subtractor_2_s0, adder_subtractor_2_s1, adder_subtractor_2_s2, adder_subtractor_2_s3;

  and A0B0 (A0B0_out, A0, B0);
  and A1B0 (A1B0_out, A1, B0);
  and A2B0 (A2B0_out, A2, B0);
  and A3B0 (A3B0_out, A3, B0);
  and A0B1 (A0B1_out, A0, B1);
  and A1B1 (A1B1_out, A1, B1);
  and A2B1 (A2B1_out, A2, B1);
  Adder_Subtractor adder_subtractor_1 (
    .Subtract(1'b0), .A0(A0B0_out), .A1(A1B0_out), .A2(A2B0_out), .A3(A3B0_out), .B0(1'b0), .B1(A0B1_out),
    .B2(A1B1_out), .B3(A2B1_out), .S0(adder_subtractor_1_s0), .S1(adder_subtractor_1_s1),
    .S2(adder_subtractor_1_s2), .S3(adder_subtractor_1_s3));
  and A0B2 (A0B2_out, A0, B2);
  and A1B2 (A1B2_out, A1, B2);
  and A0B3 (A0B3_out, A0, B3);
  Adder_Subtractor adder_subtractor_2 (
    .Subtract(1'b0), .A0(adder_subtractor_1_s0), .A1(adder_subtractor_1_s1), .A2(adder_subtractor_1_s2),
    .A3(adder_subtractor_1_s3), .B0(1'b0), .B1(1'b0), .B2(A0B2_out), .B3(A1B2_out),
    .S0(adder_subtractor_2_s0), .S1(adder_subtractor_2_s1), .S2(adder_subtractor_2_s2),
    .S3(adder_subtractor_2_s3));
  Adder_Subtractor adder_subtractor_3 (
    .Subtract(1'b0), .A0(adder_subtractor_2_s0), .A1(adder_subtractor_2_s1), .A2(adder_subtractor_2_s2),
    .A3(adder_subtractor_2_s3), .B0(1'b0), .B1(1'b0), .B2(1'b0), .B3(A0B3_out), .S0(S0), .S1(S1), .S2(S2),
    .S3(S3));
endmodule

module _5_bit_Subtractor (
  input  A0,
  input  A1,
  input  A2,
  input  A3,
  input  A4,
  input  B0,
  input  B1,
  input  B2,
  input  B3,
  input  B4,
  output out_11,
  output out_12,
  output out_13,
  output out_14,
  output out_15
);

  wire adder_1_carryout, adder_2_carryout, adder_3_carryout, adder_4_carryout, adder_5_carryout, not_1_out,
       not_2_out, not_3_out, not_4_out, not_5_out;

  not not_1 (not_1_out, B0);
  not not_2 (not_2_out, B1);
  not not_3 (not_3_out, B2);
  not not_4 (not_4_out, B3);
  not not_5 (not_5_out, B4);
  Adder adder_1 (.A(A0), .B(not_1_out), .CarryIn(1'b1), .SUM(out_11), .CarryOut(adder_1_carryout));
  Adder adder_2 (.A(A1), .B(not_2_out), .CarryIn(adder_1_carryout), .SUM(out_12), .CarryOut(adder_2_carryout));
  Adder adder_3 (.A(A2), .B(not_3_out), .CarryIn(adder_2_carryout), .SUM(out_13), .CarryOut(adder_3_carryout));
  Adder adder_4 (.A(A3), .B(not_4_out), .CarryIn(adder_3_carryout), .SUM(out_14), .CarryOut(adder_4_carryout));
  Adder adder_5 (.A(A4), .B(not_5_out), .CarryIn(adder_4_carryout), .SUM(out_15), .CarryOut(adder_5_carryout));
  // also tied to GND on the sheet: adder_5_carryout
endmodule

module Divisor (
  input  B_Conditions,
  input  A0,
  input  A1,
  input  A2,
  input  A3,
  input  B0,
  input  B1,
  input  B2,
  input  B3,
  output A_prime_0,
  output A_prime_1,
  output A_prime_2,
  output C,
  output A_prime_3
);

  wire and_1_out, and_2_out, and_3_out, and_4_out, and_5_out, and_6_out, and_7_out, and_8_out, and_9_out,
       and_10_out, and_11_out, and_12_out, n5_bit_subtractor_1_out_11, n5_bit_subtractor_1_out_12,
       n5_bit_subtractor_1_out_13, n5_bit_subtractor_1_out_14, n5_bit_subtractor_1_out_15, not_1_out;

  and and_1 (and_1_out, B0, B_Conditions);
  and and_2 (and_2_out, B1, B_Conditions);
  and and_3 (and_3_out, B2, B_Conditions);
  and and_4 (and_4_out, B3, B_Conditions);
  _5_bit_Subtractor u_5_bit_subtractor_1 (
    .A0(A0), .A1(A1), .A2(A2), .A3(A3), .A4(1'b0), .B0(and_1_out), .B1(and_2_out), .B2(and_3_out),
    .B3(and_4_out), .B4(1'b0), .out_11(n5_bit_subtractor_1_out_11), .out_12(n5_bit_subtractor_1_out_12),
    .out_13(n5_bit_subtractor_1_out_13), .out_14(n5_bit_subtractor_1_out_14),
    .out_15(n5_bit_subtractor_1_out_15));
  not not_1 (not_1_out, n5_bit_subtractor_1_out_15);
  and and_5 (and_5_out, A0, n5_bit_subtractor_1_out_15);
  and and_6 (and_6_out, A1, n5_bit_subtractor_1_out_15);
  and and_7 (and_7_out, A2, n5_bit_subtractor_1_out_15);
  and and_8 (and_8_out, A3, n5_bit_subtractor_1_out_15);
  and and_9 (and_9_out, not_1_out, n5_bit_subtractor_1_out_11);
  and and_10 (and_10_out, not_1_out, n5_bit_subtractor_1_out_12);
  and and_11 (and_11_out, not_1_out, n5_bit_subtractor_1_out_13);
  and and_12 (and_12_out, not_1_out, n5_bit_subtractor_1_out_14);
  and and_13 (C, B_Conditions, not_1_out);
  or or_1 (A_prime_0, and_5_out, and_9_out);
  or or_2 (A_prime_1, and_6_out, and_10_out);
  or or_3 (A_prime_2, and_7_out, and_11_out);
  or or_4 (A_prime_3, and_8_out, and_12_out);
endmodule

module Full_Divisor (
  input  A0,
  input  A1,
  input  A2,
  input  A3,
  input  B0,
  input  B1,
  input  B2,
  input  B3,
  output C3,
  output C2,
  output C1,
  output C0
);

  wire and_1_out, and_2_out, divisor_1_a_prime_0, divisor_1_a_prime_1, divisor_1_a_prime_2,
       divisor_1_a_prime_3, divisor_2_a_prime_0, divisor_2_a_prime_1, divisor_2_a_prime_2,
       divisor_2_a_prime_3, divisor_3_a_prime_0, divisor_3_a_prime_1, divisor_3_a_prime_2,
       divisor_3_a_prime_3, divisor_4_a_prime_0, divisor_4_a_prime_1, divisor_4_a_prime_2,
       divisor_4_a_prime_3, not_1_out, not_2_out, not_3_out;

  and and_1 (and_1_out, not_1_out, and_2_out);
  not not_1 (not_1_out, B1);
  not not_2 (not_2_out, B2);
  not not_3 (not_3_out, B3);
  Divisor divisor_1 (
    .B_Conditions(and_1_out), .A0(A0), .A1(A1), .A2(A2), .A3(A3), .B0(1'b0), .B1(1'b0), .B2(1'b0), .B3(B0),
    .A_prime_0(divisor_1_a_prime_0), .A_prime_1(divisor_1_a_prime_1), .A_prime_2(divisor_1_a_prime_2),
    .C(C3), .A_prime_3(divisor_1_a_prime_3));
  and and_2 (and_2_out, not_2_out, not_3_out);
  Divisor divisor_2 (
    .B_Conditions(and_2_out), .A0(divisor_1_a_prime_0), .A1(divisor_1_a_prime_1), .A2(divisor_1_a_prime_2),
    .A3(divisor_1_a_prime_3), .B0(1'b0), .B1(1'b0), .B2(B0), .B3(B1), .A_prime_0(divisor_2_a_prime_0),
    .A_prime_1(divisor_2_a_prime_1), .A_prime_2(divisor_2_a_prime_2), .C(C2), .A_prime_3(divisor_2_a_prime_3));
  Divisor divisor_3 (
    .B_Conditions(not_3_out), .A0(divisor_2_a_prime_0), .A1(divisor_2_a_prime_1), .A2(divisor_2_a_prime_2),
    .A3(divisor_2_a_prime_3), .B0(1'b0), .B1(B0), .B2(B1), .B3(B2), .A_prime_0(divisor_3_a_prime_0),
    .A_prime_1(divisor_3_a_prime_1), .A_prime_2(divisor_3_a_prime_2), .C(C1), .A_prime_3(divisor_3_a_prime_3));
  Divisor divisor_4 (
    .B_Conditions(1'b1), .A0(divisor_3_a_prime_0), .A1(divisor_3_a_prime_1), .A2(divisor_3_a_prime_2),
    .A3(divisor_3_a_prime_3), .B0(B0), .B1(B1), .B2(B2), .B3(B3), .A_prime_0(divisor_4_a_prime_0),
    .A_prime_1(divisor_4_a_prime_1), .A_prime_2(divisor_4_a_prime_2), .C(C0), .A_prime_3(divisor_4_a_prime_3));
  // also tied to GND on the sheet: {divisor_4_a_prime_0, divisor_4_a_prime_1, divisor_4_a_prime_2, divisor_4_a_prime_3}

  // Notes on the sheet:
  //   Remainders
endmodule
